# Fritzing sketch Sockets (saved by Fritzing 0.9.3b)

parts:
  Part1 = Arduino Uno (Rev3)
  U1 = 8RelayModule
  VCC_7+ = DC-DC CONVERTER [part_number=80633 package=dc-dc_converter]
  U5 = Power Outlet [chip_label=IC package="SIP (Single Inline) [THT]"]
  U3 = Power Outlet [chip_label=IC package="SIP (Single Inline) [THT]"]
  U4 = Power Outlet [chip_label=IC package="SIP (Single Inline) [THT]"]
  U2 = Power Outlet [chip_label=IC package="SIP (Single Inline) [THT]"]

nets:
  N1: Part1.A0, U1.IN5
  N2: Part1.A1, U1.IN6
  N3: Part1.A2, U1.IN7
  N4: Part1.A3, U1.IN8
  N5: Part1.D2, U1.IN4
  N6: Part1.D3_PWM, U1.IN3
  N7: Part1.D4, U1.IN2
  N8: Part1.D5_PWM, U1.IN1
  5V: Part1.5V, U1.VCC
  GND: Part1.GND, U1.GND, VCC_7+.OUT-
  N9: Part1.VIN, VCC_7+.OUT+
  N10: U1.NC1, U1.NC2, U1.NC3, U1.NC4, U1.NC5, U1.NC6, U1.NC7, U1.NC8
  N11: U1.NO1, U4.hot2
  N12: U1.NO2, U4.hot1
  N13: U1.NO3, U5.hot2
  N14: U1.NO4, U5.hot1
  N15: U1.NO5, U2.hot2
  N16: U1.NO6, U2.hot1
  N17: U1.NO7, U3.hot2
  N18: U1.NO8, U3.hot1
  N19: U5.neutral2, U3.neutral1, U3.neutral2, U4.neutral1, U4.neutral2, U2.neutral1, U2.neutral2

notes:
  AC INPUT
  2
  1
  3
  4
  5
  6
  7
  8

custom parts:
  8RelayModule: 8 relay arduino module SONGLE SRD05VDC-SL-C
  DC-DC CONVERTER: WYHP 5A constant current/voltage manufactured by Shenzhen Weiyapuhua Technology Co., Ltd
  Power Outlet: A standard power outlet. Silver screws are neutral, brass screws are hot. Green screw is ground.
